# Fritzing sketch Maquina de Estados Finitos (saved by Fritzing 0.9.3b)
breadboards: 1

parts:
  LCD1 = LCD screen
  Mod1 = KY-013 Analog Temperature Sensor Module [package="Breakout board"]
  Mod2 = KY-018 Photoresistor Module [package="Breakout board"]
  R1 = Rotary Potentiometer (Large) [maximum_resistance=100kΩ package=THT]
  Componente1 = Arduino Mega 2560 (Rev3)
  LED1 = RGB LED - (4 legs) [package="5 mm [THT]"]
  Componente2 = Passive Buzzer
  Keypad4x1 = Keypad Membran 4x4
  PART2 = Sound Detector

nets:
  GND: LCD1.VSS, LCD1.R/W, LCD1.LED-, Mod1.-, Mod2.-, R1.leg1, Componente1.GND, Componente2.GND, PART2.GND
  VIN: LCD1.VDD, LCD1.LED+, Mod1.Vin, Mod2.Vin, R1.leg2, Componente1.5V, LED1.common_anode, Componente2.NC
  N1: LCD1.V0, R1.wiper
  N2: LCD1.RS, Componente1.D12_PWM
  N3: LCD1.E, Componente1.D11_PWM
  N4: LCD1.DB4, Componente1.D5_PWM
  N5: LCD1.DB5, Componente1.D4_PWM
  N6: LCD1.DB6, Componente1.D3_PWM
  N7: LCD1.DB7, Componente1.D2_PWM
  N8: Mod1.S, Componente1.A0
  N9: Mod2.S, Componente1.A1
  N10: Componente1.D9_PWM, LED1.red_cathode
  N11: Componente1.D8_PWM, LED1.green_cathode
  N12: Componente1.D7_PWM, LED1.blue_cathode
  N13: Componente1.D40, Keypad4x1.Pin5
  N14: Componente1.D41, Keypad4x1.Pin1
  N15: Componente1.D42, Keypad4x1.Pin6
  N16: Componente1.D43, Keypad4x1.Pin2
  N17: Componente1.D44, Keypad4x1.Pin7
  N18: Componente1.D45, Keypad4x1.Pin3
  N19: Componente1.D47, Keypad4x1.Pin4
  N20: Componente1.D50, Componente2.S

custom parts:
  KY-013 Analog Temperature Sensor Module: KY-013 Analog Temperature Sensor module, measures ambient temperature based on resistance of the thermistor.
  KY-018 Photoresistor Module: KY-018 Photoresistor module, used to measure light intensity. It can determine the presence or absence of light.
  Keypad Membran 4x4: Membrane Keypad 4x4 Matrix
  Sound Detector: Electret microphone with multiple outputs. - First output is the actual audio - Second output is the amplitude envelope - Third output is a binary "sound present" indication - high while sound is present, low otherwise. Visit sparkfun.com for more documentations.
